# Fritzing sketch wiring (saved by Fritzing 1.0.3b)

parts:
  Mod1 = Raspberry Pi 4B
  Part1 = Arduino Nano (Rev3.0) (ICSP)
  LED1 = LED - 5mm [color="Red (633nm)" current=0.030A package="5 mm [THT]"]
  LED2 = LED - 5mm [color="Blue (525nm)" current=0.030A package="5 mm [THT]"]
  LED3 = LED - 5mm [color="Red (633nm)" current=0.030A package="5 mm [THT]"]
  LED4 = LED - 5mm [color="Red (633nm)" current=0.030A package="5 mm [THT]"]
  LED5 = LED - 5mm [color="Red (633nm)" current=0.030A package="5 mm [THT]"]
  LED6 = LED - 5mm [color="Red (633nm)" current=0.030A package="5 mm [THT]"]
  LED7 = LED - 5mm [color="Green (560nm)" current=0.030A package="5 mm [THT]"]
  SP1 = SPEAKER [package=pcb_mount_speaker]  # not connected
  SP2 = SPEAKER [package=pcb_mount_speaker]  # not connected
  S1 = Round Pushbutton  # not connected

nets:
  N1: Mod1.3V3, LED2.cathode
  N2: Mod1.GPIO2, LED7.cathode
  N3: Mod1.GPIO5, LED1.cathode
  N4: Mod1.GPIO6, LED3.cathode
  N5: Mod1.GPIO13, LED4.cathode
  N6: Mod1.GPIO19, LED5.cathode
  N7: Mod1.GPIO26, LED6.cathode
  GND: Mod1.GND, Part1.GND

notes:
  Trap
